# Fritzing sketch board (saved by Fritzing 0.8.7b)
circuit board: 6.88566cm x 5.36311cm
breadboards: 1

parts:
  J1 = Basic Servo
  U1 = Voltage Regulator - 5V [package="TO220 [THT]"]
  V1 = DC Power [voltage=12V]  # not connected
  Bauteil1 = Arduino Leonardo (Rev3b)
  J2 = Screw terminal - 2 pins [package=THT]
  C1 = Electrolytic Capacitor [capacitance=1µF package="100 mil [THT, electrolytic]"]
  C2 = Electrolytic Capacitor [capacitance=100nF voltage=20V package="100 mil [THT, electrolytic]"]
  J3 = female pin header, 2 pins [form="♀ (female)"]
  JP3 = Header 10 [part_number="RN-171, P 1-10" package=1x10-2mm-smd]
  JP1 = Header 10 [part_number="RN-171, P11-20" package=1x10-2mm-smd]  # not connected
  Bauteil4 = Tri-Axis Gyro Breakout - L3G4200D [part_number=Gyro-Sensor]
  JP4 = Header 1 [package=1x01_offset]
  JP5 = Header 1 [package=1x01_offset]
  JP6 = Header 1 [package=1x01_offset]
  JP7 = Header 1 [package=1x01_offset]
  U3 = MMA_ACCEL_CONNECTOR [package=1x08]  # not connected
  VCC1 = Battery block 9V
  Pololu_A1 = Pololu A4988 [package=SO16]  # not connected
  Pololu_A2 = Pololu A4988 [package=SO16]
  JP9 = M10X2 [package=2x10_lock]  # not connected
  U4 = M10X2 [package=2x10_lock]  # not connected
  J4 = female pin header, 2 pins [form="♀ (female)" part_number=MS1-1]
  J5 = female pin header, 2 pins [form="♀ (female)"]
  J6 = female pin header, 2 pins [form="♀ (female)"]
  C3 = Electrolytic Capacitor [capacitance=47µF voltage=16V part_number=100uF package="100 mil [THT, electrolytic]"]
  J7 = screw terminal, 4 pins

nets:
  GND: J1.gnd, U1.GND, Bauteil1.GND, J2.pin2, C1.-, C2.-, JP3.1, Bauteil4.GND, JP5.1, VCC1.-, Pololu_A2.GND, J4.pin1, J5.pin2, J6.pin1, C3.-
  VCC: J1.vcc, U1.output_voltage, C1.+, Bauteil4.VCC, JP4.1
  N1: J1.pulse, Bauteil1.D5_PWM
  N2: U1.input_voltage, Bauteil1.VIN, J2.pin1, C2.+, VCC1.+, Pololu_A2.VMOT, C3.+
  N3: Bauteil1.D0/RX, JP3.9
  N4: Bauteil1.D1/TX, JP3.8
  N5: Bauteil1.D4/A6, Pololu_A2.ENABLE
  N6: Bauteil1.D6_PWM/A7, Pololu_A2.STEP
  N7: Bauteil1.3V3, JP3.10
  5V: Bauteil1.5V, Pololu_A2.VDD
  N8: Bauteil1.A0, J3.pin1
  N9: Bauteil1.D8/A8, Pololu_A2.DIR
  N10: Bauteil1.SDA, Bauteil4.SDA, JP7.1
  N11: Bauteil1.SCL, Bauteil4.SCL, JP6.1
  N12: Pololu_A2.MS1, J4.pin2
  N13: Pololu_A2.MS2, J5.pin1
  N14: Pololu_A2.MS3, J6.pin2
  N15: Pololu_A2.RESET, Pololu_A2.SLEEP
  N16: Pololu_A2.1B, J7.pin4
  N17: Pololu_A2.1A, J7.pin3
  N18: Pololu_A2.2A, J7.pin2
  N19: Pololu_A2.2B, J7.pin1

notes:
  RN-171

custom parts:
  M10X2: This was SPECIALLY designed to be used with our Graphic LCD Backpack. Be sure you want to use this! It is not only staggered on each line of header holes, but IT IS ALSO offset of the center point of the top and bottom lines by 5 mil. This causes the headers to lock into place on the standard footprint on the LCD screen. The extra squares on the tdocu layer are there simply to reference other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
